// Logisim project ExampleCircuit.circ as structural Verilog: 1 circuit, main circuit main
module main (
  input  [5:0] in_1
);

  wire n6to14_1_a1, n6to14_1_a_2, n6to14_1_b1, n6to14_1_b_2, n6to14_1_c1, n6to14_1_c_2, n6to14_1_d1,
       n6to14_1_d_2, n6to14_1_e1, n6to14_1_e_2, n6to14_1_f1, n6to14_1_f_2, n6to14_1_g, n6to14_1_g1;

  _7_Segment_Display u_7_segment_display_1 (
    .g(n6to14_1_g1), .f(n6to14_1_f1), .a(n6to14_1_a1), .b(n6to14_1_b1), .e(n6to14_1_e1), .d(n6to14_1_d1),
    .c(n6to14_1_c1));  // open: dp
  _6to14 u_6to14_1 (
    .F(in_1[0]), .E(in_1[1]), .D(in_1[2]), .C(in_1[3]), .B(in_1[4]), .A(in_1[5]), .A1(n6to14_1_a1),
    .F1(n6to14_1_f1), .B1(n6to14_1_b1), .G1(n6to14_1_g1), .E1(n6to14_1_e1), .D1(n6to14_1_d1),
    .C1(n6to14_1_c1), .A_2(n6to14_1_a_2), .F_2(n6to14_1_f_2), .B_2(n6to14_1_b_2), .G(n6to14_1_g),
    .E_2(n6to14_1_e_2), .D_2(n6to14_1_d_2), .C_2(n6to14_1_c_2));
  _7_Segment_Display u_7_segment_display_2 (
    .g(n6to14_1_g), .f(n6to14_1_f_2), .a(n6to14_1_a_2), .b(n6to14_1_b_2), .e(n6to14_1_e_2), .d(n6to14_1_d_2),
    .c(n6to14_1_c_2));  // open: dp
endmodule
